// Logisim project RPS.circ as structural Verilog: 1 circuit, main circuit main
module main (
  input  Rock,
  input  Paper,
  input  Scissors,
  input  Rock_2,
  input  Paper_2,
  input  Scissors_2,
  output Player_A_Wins,
  output Player_B_Wins,
  output INVALID_INPUT__SELECT_ONE_OPTION
);

  wire and_1_out, and_2_out, and_3_out, and_4_out, and_5_out, and_6_out, and_7_out, and_8_out, and_9_out,
       and_10_out, or_1_out, or_2_out;

  and and_1 (and_1_out, Rock, Rock, Paper_2);
  and and_2 (and_2_out, Rock, Scissors_2);
  and and_3 (and_3_out, Paper, Rock_2);
  and and_4 (and_4_out, Paper, Scissors_2, Scissors_2);
  and and_5 (and_5_out, Rock, Paper);
  and and_6 (and_6_out, Scissors, Rock);
  and and_7 (and_7_out, Paper, Scissors);
  and and_8 (and_8_out, Rock_2, Paper_2);
  and and_9 (and_9_out, Rock_2, Scissors_2);
  and and_10 (and_10_out, Paper_2, Scissors_2);
  or or_1 (or_1_out, and_5_out, and_6_out, and_7_out);
  or or_2 (or_2_out, and_8_out, and_10_out, and_9_out);
  or or_3 (INVALID_INPUT__SELECT_ONE_OPTION, or_1_out, or_2_out);
  or or_4 (Player_A_Wins, and_2_out, and_3_out);
  or or_5 (Player_B_Wins, and_1_out, and_4_out);

  // Notes on the sheet:
  //   Player A
  //   Player B
endmodule
